# Fritzing sketch Prototype v1 sketch (saved by Fritzing 0.9.3b)

parts:
  Part1 = Arduino Mega 2560 (Rev3)
  MPU9250_MPU-1 = SparkFun IMU Breakout - MPU-9250 [part_number=" SEN-13762"]

nets:
  N1: Part1.D21/SCL, MPU9250_MPU-1.SCL/SCLK
  N2: Part1.D20/SDA, MPU9250_MPU-1.SDA/SDI
  5V: Part1.5V, MPU9250_MPU-1.VDD
  GND: Part1.GND, MPU9250_MPU-1.GND
